# Fritzing sketch MAX7219-788BS-LEDs (saved by Fritzing 0.9.2b)
breadboards: 1

parts:
  MAX7219 = MAX7219 [package=dil24]
  788BS = LBT2088AH [part_number=LBT2088AH]
  C3 = Ceramic Capacitor [capacitance=10µF package="100 mil [THT, multilayer]"]
  C4 = Ceramic Capacitor [capacitance=0.1µF package="100 mil [THT, multilayer]"]
  R2 = Resistor [tolerance=±5% resistance=33k package=THT]
  R3 = Resistor [tolerance=±5% resistance=10k package=THT]
  JP1 = Header 3 [package=1x03-1mm-ra]

nets:
  N1: MAX7219.DIN, JP1.MOSI
  N2: MAX7219.DIG0, 788BS.pin_13
  N3: MAX7219.DIG4, 788BS.pin_6
  GND: MAX7219.GND, MAX7219.GND2, C3.0, C4.0, R3.Pin_1
  N4: MAX7219.DIG6, 788BS.pin_15
  N5: MAX7219.DIG2, 788BS.pin_4
  N6: MAX7219.DIG3, 788BS.pin_10
  N7: MAX7219.DIG7, 788BS.pin_16
  N8: MAX7219.DIG5, 788BS.pin_11
  N9: MAX7219.DIG1, 788BS.pin_3
  N10: MAX7219.LOAD, R3.Pin_0, JP1.SS
  N11: MAX7219.CLK, JP1.SCK
  N12: MAX7219.SEGA, 788BS.pin2
  N13: MAX7219.SEGF, 788BS.pin_14
  N14: MAX7219.SEGB, 788BS.pin_7
  N15: MAX7219.SEGG, 788BS.pin_9
  N16: MAX7219.ISET, R2.Pin_0
  5V: MAX7219.VCC, C3.1, C4.1, R2.Pin_1
  N17: MAX7219.SEGC, 788BS.pin1
  N18: MAX7219.SEGE, 788BS.pin_8
  N19: MAX7219.SEGDP, 788BS.pin_5
  N20: MAX7219.SEGD, 788BS.pin_12

custom parts:
  MAX7219: 8-digit, 8-segment LED display driver, serial input
  Header 3: Header 3 Standard 3-pin 0.1 header. Use with straight break away headers (SKU : PRT-00116), right angle break away headers (PRT-00553), swiss pins (PRT-00743), machine pins (PRT-00117), and female headers (PRT-00115). Molex polarized connector foot print use with SKU : PRT-08232 with associated crimp pins and housings.
