# Fritzing sketch MAX7219-788BS (saved by Fritzing 0.9.2b)
breadboards: 1

parts:
  MAX7219 = IC, DIP package, 24 pins [chip_label=IC]
  788BS = IC, DIP package, 16 pins [chip_label=IC]
  C1 = Ceramic Capacitor [capacitance=10µF package="100 mil [THT, multilayer]"]
  C2 = Ceramic Capacitor [capacitance=0.1µF package="100 mil [THT, multilayer]"]
  R1 = Resistor [tolerance=±5% resistance=28k package=THT]
  (x_x) = Header 3 [package=1x03-1mm-ra]

nets:
  N1: MAX7219.pin1, (x_x).MOSI
  N2: MAX7219.pin2, 788BS.pin13
  N3: MAX7219.pin3, 788BS.pin6
  GND: MAX7219.pin4, MAX7219.pin9, C1.0, C2.0
  N4: MAX7219.pin5, 788BS.pin15
  N5: MAX7219.pin6, 788BS.pin4
  N6: MAX7219.pin7, 788BS.pin10
  N7: MAX7219.pin8, 788BS.pin16
  N8: MAX7219.pin10, 788BS.pin11
  N9: MAX7219.pin11, 788BS.pin3
  N10: MAX7219.pin12, (x_x).SS
  N11: MAX7219.pin13, (x_x).SCK
  N12: MAX7219.pin14, 788BS.pin2
  N13: MAX7219.pin15, 788BS.pin14
  N14: MAX7219.pin16, 788BS.pin7
  N15: MAX7219.pin17, 788BS.pin9
  N16: MAX7219.pin18, R1.Pin_1
  5V: MAX7219.pin19, C1.1, C2.1, R1.Pin_0
  N17: MAX7219.pin20, 788BS.pin1
  N18: MAX7219.pin21, 788BS.pin8
  N19: MAX7219.pin22, 788BS.pin5
  N20: MAX7219.pin23, 788BS.pin12

notes:
  MOSI - connect to pin 51 on Arduino Mega
  SCK - connect to pin 52 on Arduino Mega
  SS - connect ot porper Digital Out on Arduino (see LED_Display.fzz)
  Use externa power source for 5V (not from Arduino)

custom parts:
  Header 3: Header 3 Standard 3-pin 0.1 header. Use with straight break away headers (SKU : PRT-00116), right angle break away headers (PRT-00553), swiss pins (PRT-00743), machine pins (PRT-00117), and female headers (PRT-00115). Molex polarized connector foot print use with SKU : PRT-08232 with associated crimp pins and housings.
